# Fritzing sketch fritzcircuit29 (saved by Fritzing 0.9.4)
breadboards: 1

parts:
  Raspberry_Pi_1 = Raspberry Pi 3 [part_number=RPI-3-V1.2]
  LED1 = LED - 5mm [color="Red (633nm)" package="5 mm [THT]"]
  LED2 = LED - 5mm [color="Red (633nm)" package="5 mm [THT]"]
  R3 = Resistor [tolerance=±5% resistance=220 package="1206 [SMD]"]
  J1 = Basic Servo

nets:
  3V3: Raspberry_Pi_1.3v3, J1.vcc
  N1: Raspberry_Pi_1.GIPO17, J1.pulse
  N2: Raspberry_Pi_1.GIPO27, LED1.anode
  N3: Raspberry_Pi_1.GIPO22, LED2.anode
  GND: Raspberry_Pi_1.GND, R3.Pin_1, J1.gnd
  N4: LED1.cathode, LED2.cathode, R3.Pin_0
